// Logisim project L0_FSM.circ as structural Verilog: 3 circuits, main circuit fsm
module fsm (
  input  in_1,
  input  [1:0] in_2,
  output out_3
);

  wire clock_1_out;
  wire [1:0] multiplexer_1_out, register_1_q, \状态转移_1_out_3 ;

  // Probe on \状态转移_1_out_3 
  \状态转移  \u_状态转移_1  (.in_1(register_1_q), .in_2(in_2), .out_3(\状态转移_1_out_3 ));
  // Probe on multiplexer_1_out
  Multiplexer #(.width(2)) multiplexer_1 (
    .in0(\状态转移_1_out_3 ), .in1(2'b00), .out(multiplexer_1_out), .sel(in_1));  // open: en
  Clock clock_1 (.out(clock_1_out));
  Register #(.width(2)) register_1 (.D(multiplexer_1_out), .Q(register_1_q), .clk(clock_1_out));  // open: en, clr
  \输出  \u_输出_1  (.in_1(register_1_q), .in_2(in_2), .o(out_3));
endmodule

module \状态转移  (
  input  [1:0] in_1,
  input  [1:0] in_2,
  output [1:0] out_3
);

  wire and_1_out, and_2_out, and_3_out, and_4_out, and_5_out, and_6_out, and_7_out, and_8_out, not_1_out,
       not_2_out, not_3_out, not_4_out, not_5_out, not_6_out, not_7_out, not_8_out, not_9_out, not_10_out,
       not_11_out, not_12_out, not_13_out, not_14_out, not_15_out, not_16_out;

  not not_1 (not_1_out, in_1[1]);
  and and_1 (and_1_out, not_1_out, in_1[0], not_2_out);
  not not_2 (not_2_out, in_2[1]);
  not not_3 (not_3_out, in_1[1]);
  and and_2 (and_2_out, not_3_out, in_1[0], not_4_out);
  not not_4 (not_4_out, in_2[0]);
  and and_3 (and_3_out, in_1[1], not_5_out, not_6_out);
  not not_5 (not_5_out, in_1[0]);
  not not_6 (not_6_out, in_2[1]);
  and and_4 (and_4_out, in_1[1], not_7_out, not_8_out);
  not not_7 (not_7_out, in_1[0]);
  not not_8 (not_8_out, in_2[0]);
  not not_9 (not_9_out, in_1[1]);
  not not_10 (not_10_out, in_1[0]);
  not not_11 (not_11_out, in_2[1]);
  not not_12 (not_12_out, in_1[1]);
  not not_13 (not_13_out, in_2[0]);
  not not_14 (not_14_out, in_1[0]);
  not not_15 (not_15_out, in_2[0]);
  not not_16 (not_16_out, in_2[1]);
  or or_1 (out_3[1], and_1_out, and_2_out, and_3_out, and_4_out);
  and and_5 (and_5_out, not_9_out, not_10_out, not_11_out, in_2[0]);
  and and_6 (and_6_out, not_12_out, in_1[0], not_13_out);
  and and_7 (and_7_out, in_1[1], not_14_out, not_15_out);
  and and_8 (and_8_out, in_1[1], in_1[0], not_16_out, in_2[0]);
  or or_2 (out_3[0], and_5_out, and_6_out, and_7_out, and_8_out);
endmodule

module \输出  (
  input  [1:0] in_1,
  input  [1:0] in_2,
  output o
);

  wire not_1_out;

  not not_1 (not_1_out, in_2[0]);
  and and_1 (o, in_1[1], in_1[0], not_1_out);
endmodule
