// Logisim project P0_L0_CRC.circ as structural Verilog: 2 circuits, main circuit CRC
module CRC (
  input  [7:0] in_1,
  input  [3:0] B,
  output [10:0] out_3
);

  wire [3:0] xor_1_out, xor_2_out, xor_3_out, xor_4_out;
  wire [3:3] xor_5_out;

  // Probe on in_1
  assign xor_1_out = in_1[7:4] ^ B;  // XOR_Gate xor_1, 4 bits wide
  assign xor_2_out = {xor_1_out[2:0], in_1[3]} ^ B;  // XOR_Gate xor_2, 4 bits wide
  assign xor_3_out = {xor_2_out[2:0], in_1[2]} ^ B;  // XOR_Gate xor_3, 4 bits wide
  assign xor_4_out = {xor_3_out[2:0], in_1[1]} ^ B;  // XOR_Gate xor_4, 4 bits wide
  assign {xor_5_out[3], out_3[2:0]} = {xor_4_out[2:0], in_1[0]} ^ B;  // XOR_Gate xor_5, 4 bits wide

  assign out_3[10:3] = in_1;
endmodule

module \计算  (
  input  in_1,
  input  [3:0] in_2,
  input  [3:0] in_3,
  output [3:0] out_4
);

  wire [3:3] xor_1_out;

  assign {xor_1_out[3], out_4[3:1]} = in_2 ^ in_3;  // XOR_Gate xor_1, 4 bits wide

  assign out_4[0] = in_1;
endmodule
