// Logisim project P0_L0_CRC_2.circ as structural Verilog: 2 circuits, main circuit CRC
module CRC (
  input  [7:0] in_1,
  input  [3:0] B,
  output [10:0] out_3
);

  wire [0:0] \计算_8_out_4 ;
  wire [3:0] \计算_1_out_4 , \计算_2_out_4 , \计算_3_out_4 , \计算_4_out_4 , \计算_5_out_4 , \计算_6_out_4 , \计算_7_out_4 ;

  // Probe on in_1
  // Probe on \计算_1_out_4 
  \计算  \u_计算_1  (.in_1(in_1[3]), .in_2(in_1[7:4]), .in_3(B), .out_4(\计算_1_out_4 ));
  \计算  \u_计算_2  (.in_1(in_1[2]), .in_2(\计算_1_out_4 ), .in_3(B), .out_4(\计算_2_out_4 ));
  \计算  \u_计算_3  (.in_1(in_1[1]), .in_2(\计算_2_out_4 ), .in_3(B), .out_4(\计算_3_out_4 ));
  \计算  \u_计算_4  (.in_1(in_1[0]), .in_2(\计算_3_out_4 ), .in_3(B), .out_4(\计算_4_out_4 ));
  \计算  \u_计算_5  (.in_1(1'b0), .in_2(\计算_4_out_4 ), .in_3(B), .out_4(\计算_5_out_4 ));
  \计算  \u_计算_6  (.in_1(1'b0), .in_2(\计算_5_out_4 ), .in_3(B), .out_4(\计算_6_out_4 ));
  \计算  \u_计算_7  (.in_1(1'b0), .in_2(\计算_6_out_4 ), .in_3(B), .out_4(\计算_7_out_4 ));
  \计算  \u_计算_8  (.in_1(1'b0), .in_2(\计算_7_out_4 ), .in_3(B), .out_4({out_3[2:0], \计算_8_out_4 [0]}));

  assign out_3[10:3] = in_1;
endmodule

module \计算  (
  input  in_1,
  input  [3:0] in_2,
  input  [3:0] in_3,
  output [3:0] out_4
);

  wire [3:0] xor_1_out;

  assign xor_1_out = in_2 ^ in_3;  // XOR_Gate xor_1, 4 bits wide
  Multiplexer #(.width(3)) multiplexer_1 (
    .in0(in_2[2:0]), .in1(xor_1_out[2:0]), .out(out_4[3:1]), .sel(in_2[3]));  // open: en

  assign out_4[0] = in_1;
endmodule
