// Logisim project P0_L1_navigation_2020.circ as structural Verilog: 4 circuits, main circuit navigation
module navigation (
  input  [1:0] in_1,
  input  in_2,
  input  in_3,
  output out_4,
  output out_5
);

  wire undriven;
  wire [2:0] register_1_q, \状态转移_1_out_3 ;
  wire [3:3] \状态转移_1_h ;

  // Probe on nothing
  \状态转移  \u_状态转移_1  (.in_1(register_1_q), .in_2(in_1), .out_3(\状态转移_1_out_3 ), .h(\状态转移_1_h [3]));
  // Probe on undriven
  // Probe on register_1_q
  Register #(.width(4)) register_1 (
    .D({\状态转移_1_h [3], \状态转移_1_out_3 }), .Q({out_5, register_1_q}), .clk(in_2), .clr(in_3));  // open: en
  \输出  \u_输出_1  (.in_1(register_1_q), .out_2(out_4));

  // Other names for the same wires on the sheet: clk = in_2; dir[1:0] = in_1; reset = in_3
endmodule

module \状态转移  (
  input  [2:0] in_1,
  input  [1:0] in_2,
  output [2:0] out_3,
  output h
);

  wire and_1_out, and_2_out, and_3_out, and_4_out, and_5_out, and_6_out, and_7_out, and_8_out, and_9_out,
       and_10_out, and_11_out, and_12_out, and_13_out, and_14_out, and_15_out, and_16_out, and_17_out,
       and_18_out, and_19_out, and_20_out, and_21_out, and_22_out, and_23_out, and_24_out, and_25_out,
       not_1_out, not_2_out, not_3_out, not_4_out, not_5_out, not_6_out, not_7_out, not_8_out, not_9_out,
       not_10_out, not_11_out, not_12_out, not_13_out, not_14_out, not_15_out, not_16_out, not_17_out,
       not_18_out, not_19_out, not_20_out, not_21_out, not_22_out, not_23_out, not_24_out, not_25_out,
       not_26_out, not_27_out, not_28_out, not_29_out, not_30_out, not_31_out, not_32_out, not_33_out;

  not not_1 (not_1_out, in_1[0]);
  not not_2 (not_2_out, in_2[1]);
  not not_3 (not_3_out, in_2[1]);
  not not_4 (not_4_out, in_2[0]);
  not not_5 (not_5_out, in_1[1]);
  not not_6 (not_6_out, in_2[1]);
  not not_7 (not_7_out, in_2[1]);
  not not_8 (not_8_out, in_1[0]);
  not not_9 (not_9_out, in_2[1]);
  not not_10 (not_10_out, in_2[0]);
  not not_11 (not_11_out, in_1[0]);
  not not_12 (not_12_out, in_2[0]);
  not not_13 (not_13_out, in_1[2]);
  not not_14 (not_14_out, in_1[1]);
  not not_15 (not_15_out, in_1[0]);
  not not_16 (not_16_out, in_2[1]);
  not not_17 (not_17_out, in_2[0]);
  not not_18 (not_18_out, in_2[0]);
  not not_19 (not_19_out, in_1[2]);
  not not_20 (not_20_out, in_1[1]);
  not not_21 (not_21_out, in_1[0]);
  not not_22 (not_22_out, in_1[2]);
  not not_23 (not_23_out, in_1[1]);
  not not_24 (not_24_out, in_1[0]);
  not not_25 (not_25_out, in_1[2]);
  not not_26 (not_26_out, in_1[1]);
  not not_27 (not_27_out, in_1[2]);
  not not_28 (not_28_out, in_1[0]);
  not not_29 (not_29_out, in_1[0]);
  not not_30 (not_30_out, in_2[1]);
  not not_31 (not_31_out, in_2[0]);
  not not_32 (not_32_out, in_2[1]);
  not not_33 (not_33_out, in_2[0]);
  and and_1 (and_1_out, in_1[1], not_1_out, not_2_out, in_2[0]);
  and and_2 (and_2_out, in_1[1], in_1[0], not_3_out, not_4_out);
  and and_3 (and_3_out, in_1[2], in_1[0]);
  and and_4 (and_4_out, in_1[2], in_1[1]);
  and and_5 (and_5_out, not_5_out, in_1[0], not_6_out);
  and and_6 (and_6_out, in_1[0], not_7_out, in_2[0]);
  and and_7 (and_7_out, in_1[1], not_8_out, not_9_out, not_10_out);
  and and_8 (and_8_out, in_1[1], not_11_out, in_2[1], in_2[0]);
  and and_9 (and_9_out, in_1[1], in_1[0], in_2[1], not_12_out);
  and and_10 (and_10_out, in_1[2], in_1[0]);
  and and_11 (and_11_out, in_1[2], in_1[1]);
  and and_12 (and_12_out, not_13_out, not_14_out, not_15_out, not_16_out, not_17_out);
  and and_13 (and_13_out, in_1[0], in_2[0]);
  and and_14 (and_14_out, in_1[1], in_2[1], not_18_out);
  and and_15 (and_15_out, in_1[2], in_1[0]);
  and and_16 (and_16_out, in_1[2], in_1[1]);
  and and_17 (and_17_out, not_19_out, not_20_out, not_21_out, in_2[0]);
  and and_18 (and_18_out, not_22_out, not_23_out, not_24_out, in_2[1]);
  and and_19 (and_19_out, not_25_out, not_26_out, in_2[1], in_2[0]);
  and and_20 (and_20_out, not_27_out, not_28_out, in_2[1], in_2[0]);
  and and_21 (and_21_out, in_1[1], not_29_out, not_30_out, not_31_out);
  and and_22 (and_22_out, in_1[1], in_1[0], not_32_out, in_2[0]);
  and and_23 (and_23_out, in_1[1], in_1[0], in_2[1], not_33_out);
  and and_24 (and_24_out, in_1[2], in_1[0]);
  and and_25 (and_25_out, in_1[2], in_1[1]);
  or or_1 (out_3[2], and_1_out, and_2_out, and_3_out, and_4_out);
  or or_2 (out_3[1], and_5_out, and_6_out, and_7_out, and_8_out, and_9_out, and_10_out, and_11_out);
  or or_3 (out_3[0], and_12_out, and_13_out, and_14_out, and_15_out, and_16_out);
  or or_4 (h, and_17_out, and_18_out, and_19_out, and_20_out, and_21_out, and_22_out, and_23_out, and_24_out, and_25_out);
endmodule

module \输出  (
  input  [2:0] in_1,
  output out_2
);

  wire comparator_1_eq;

  Comparator #(.width(3), .mode("unsigned")) comparator_1 (.a(in_1), .b(3'b100), .eq(comparator_1_eq));  // open: gt, lt
  Multiplexer multiplexer_1 (.in0(1'b0), .in1(1'b1), .out(out_2), .sel(comparator_1_eq));  // open: en
endmodule

module test (
  input  a,
  input  b,
  input  c,
  input  d,
  input  e,
  output x,
  output y,
  output z,
  output h
);

  wire and_1_out, and_2_out, and_3_out, and_4_out, and_5_out, and_6_out, and_7_out, and_8_out, and_9_out,
       and_10_out, and_11_out, and_12_out, and_13_out, and_14_out, and_15_out, and_16_out, and_17_out,
       and_18_out, and_19_out, and_20_out, and_21_out, and_22_out, and_23_out, and_24_out, and_25_out,
       not_1_out, not_2_out, not_3_out, not_4_out, not_5_out, not_6_out, not_7_out, not_8_out, not_9_out,
       not_10_out, not_11_out, not_12_out, not_13_out, not_14_out, not_15_out, not_16_out, not_17_out,
       not_18_out, not_19_out, not_20_out, not_21_out, not_22_out, not_23_out, not_24_out, not_25_out,
       not_26_out, not_27_out, not_28_out, not_29_out, not_30_out, not_31_out, not_32_out, not_33_out;

  not not_1 (not_1_out, c);
  not not_2 (not_2_out, d);
  not not_3 (not_3_out, d);
  not not_4 (not_4_out, e);
  not not_5 (not_5_out, b);
  not not_6 (not_6_out, d);
  not not_7 (not_7_out, d);
  not not_8 (not_8_out, c);
  not not_9 (not_9_out, d);
  not not_10 (not_10_out, e);
  not not_11 (not_11_out, c);
  not not_12 (not_12_out, e);
  not not_13 (not_13_out, a);
  not not_14 (not_14_out, b);
  not not_15 (not_15_out, c);
  not not_16 (not_16_out, d);
  not not_17 (not_17_out, e);
  not not_18 (not_18_out, e);
  not not_19 (not_19_out, a);
  not not_20 (not_20_out, b);
  not not_21 (not_21_out, c);
  not not_22 (not_22_out, a);
  not not_23 (not_23_out, b);
  not not_24 (not_24_out, c);
  not not_25 (not_25_out, a);
  not not_26 (not_26_out, b);
  not not_27 (not_27_out, a);
  not not_28 (not_28_out, c);
  not not_29 (not_29_out, c);
  not not_30 (not_30_out, d);
  not not_31 (not_31_out, e);
  not not_32 (not_32_out, d);
  not not_33 (not_33_out, e);
  and and_1 (and_1_out, b, not_1_out, not_2_out, e);
  and and_2 (and_2_out, b, c, not_3_out, not_4_out);
  and and_3 (and_3_out, a, c);
  and and_4 (and_4_out, a, b);
  and and_5 (and_5_out, not_5_out, c, not_6_out);
  and and_6 (and_6_out, c, not_7_out, e);
  and and_7 (and_7_out, b, not_8_out, not_9_out, not_10_out);
  and and_8 (and_8_out, b, not_11_out, d, e);
  and and_9 (and_9_out, b, c, d, not_12_out);
  and and_10 (and_10_out, a, c);
  and and_11 (and_11_out, a, b);
  and and_12 (and_12_out, not_13_out, not_14_out, not_15_out, not_16_out, not_17_out);
  and and_13 (and_13_out, c, e);
  and and_14 (and_14_out, b, d, not_18_out);
  and and_15 (and_15_out, a, c);
  and and_16 (and_16_out, a, b);
  and and_17 (and_17_out, not_19_out, not_20_out, not_21_out, e);
  and and_18 (and_18_out, not_22_out, not_23_out, not_24_out, d);
  and and_19 (and_19_out, not_25_out, not_26_out, d, e);
  and and_20 (and_20_out, not_27_out, not_28_out, d, e);
  and and_21 (and_21_out, b, not_29_out, not_30_out, not_31_out);
  and and_22 (and_22_out, b, c, not_32_out, e);
  and and_23 (and_23_out, b, c, d, not_33_out);
  and and_24 (and_24_out, a, c);
  and and_25 (and_25_out, a, b);
  or or_1 (x, and_1_out, and_2_out, and_3_out, and_4_out);
  or or_2 (y, and_5_out, and_6_out, and_7_out, and_8_out, and_9_out, and_10_out, and_11_out);
  or or_3 (z, and_12_out, and_13_out, and_14_out, and_15_out, and_16_out);
  or or_4 (h, and_17_out, and_18_out, and_19_out, and_20_out, and_21_out, and_22_out, and_23_out, and_24_out, and_25_out);
endmodule
