// Logisim project p0_L0_GRF.circ as structural Verilog: 2 circuits, main circuit grf
module grf (
  input  clk,
  input  reset,
  input  WE,
  input  [4:0] A1,
  input  [4:0] A2,
  input  [4:0] A3,
  input  [31:0] WD,
  output [31:0] out_8,
  output [31:0] out_9
);

  wire [31:0] r1, r2, r3, r4, r5, r6, r7, r8, r9, r10, r11, r12, r13, r14, r15, r16, r17, r18, r19, r20, r21,
       r22, r23, r24, r25, r26, r27, r28, r29, r30, r31, r32, r_1, r_2, r_3, r_4, r_5, r_6, r_7, r_8, r_9,
       r_10, r_11, r_12, r_13, r_14, r_15, r_16, r_17, r_18, r_19, r_20, r_21, r_22, r_23, r_24, r_25, r_26,
       r_27, r_28, r_29, r_30, r_31, r_32;

  // Probe on r_3
  Register #(.width(32)) register_1 (.Q(r1), .clk(clk), .clr(reset));  // open: D, en
  Register #(.width(32)) register_2 (.D(r_2), .Q(r2), .clk(clk), .clr(reset));  // open: en
  Register #(.width(32)) register_3 (.D(r_3), .Q(r3), .clk(clk), .clr(reset));  // open: en
  Register #(.width(32)) register_4 (.D(r_4), .Q(r4), .clk(clk), .clr(reset));  // open: en
  Register #(.width(32)) register_5 (.D(r_5), .Q(r5), .clk(clk), .clr(reset));  // open: en
  Register #(.width(32)) register_6 (.D(r_6), .Q(r6), .clk(clk), .clr(reset));  // open: en
  Register #(.width(32)) register_7 (.D(r_7), .Q(r7), .clk(clk), .clr(reset));  // open: en
  Register #(.width(32)) register_8 (.D(r_8), .Q(r8), .clk(clk), .clr(reset));  // open: en
  Register #(.width(32)) register_9 (.D(r_9), .Q(r9), .clk(clk), .clr(reset));  // open: en
  Register #(.width(32)) register_10 (.D(r_10), .Q(r10), .clk(clk), .clr(reset));  // open: en
  Register #(.width(32)) register_11 (.D(r_11), .Q(r11), .clk(clk), .clr(reset));  // open: en
  Register #(.width(32)) register_12 (.D(r_12), .Q(r12), .clk(clk), .clr(reset));  // open: en
  Register #(.width(32)) register_13 (.D(r_13), .Q(r13), .clk(clk), .clr(reset));  // open: en
  Register #(.width(32)) register_14 (.D(r_14), .Q(r14), .clk(clk), .clr(reset));  // open: en
  Register #(.width(32)) register_15 (.D(r_15), .Q(r15), .clk(clk), .clr(reset));  // open: en
  Register #(.width(32)) register_16 (.D(r_16), .Q(r16), .clk(clk), .clr(reset));  // open: en
  Register #(.width(32)) register_17 (.D(r_17), .Q(r17), .clk(clk), .clr(reset));  // open: en
  Register #(.width(32)) register_18 (.D(r_18), .Q(r18), .clk(clk), .clr(reset));  // open: en
  Register #(.width(32)) register_19 (.D(r_19), .Q(r19), .clk(clk), .clr(reset));  // open: en
  Register #(.width(32)) register_20 (.D(r_20), .Q(r20), .clk(clk), .clr(reset));  // open: en
  Register #(.width(32)) register_21 (.D(r_21), .Q(r21), .clk(clk), .clr(reset));  // open: en
  Register #(.width(32)) register_22 (.D(r_22), .Q(r22), .clk(clk), .clr(reset));  // open: en
  Register #(.width(32)) register_23 (.D(r_23), .Q(r23), .clk(clk), .clr(reset));  // open: en
  Register #(.width(32)) register_24 (.D(r_24), .Q(r24), .clk(clk), .clr(reset));  // open: en
  Register #(.width(32)) register_25 (.D(r_25), .Q(r25), .clk(clk), .clr(reset));  // open: en
  Register #(.width(32)) register_26 (.D(r_26), .Q(r26), .clk(clk), .clr(reset));  // open: en
  Register #(.width(32)) register_27 (.D(r_27), .Q(r27), .clk(clk), .clr(reset));  // open: en
  Register #(.width(32)) register_28 (.D(r_28), .Q(r28), .clk(clk), .clr(reset));  // open: en
  Register #(.width(32)) register_29 (.D(r_29), .Q(r29), .clk(clk), .clr(reset));  // open: en
  Register #(.width(32)) register_30 (.D(r_30), .Q(r30), .clk(clk), .clr(reset));  // open: en
  Register #(.width(32)) register_31 (.D(r_31), .Q(r31), .clk(clk), .clr(reset));  // open: en
  Register #(.width(32)) register_32 (.D(r_32), .Q(r32), .clk(clk), .clr(reset));  // open: en
  Multiplexer #(.select(5), .width(32)) multiplexer_1 (
    .in0(r1), .in1(r2), .in2(r3), .in3(r4), .in4(r5), .in5(r6), .in6(r7), .in7(r8), .in8(r9), .in9(r10),
    .in10(r11), .in11(r12), .in12(r13), .in13(r14), .in14(r15), .in15(r16), .in16(r17), .in17(r18),
    .in18(r19), .in19(r20), .in20(r21), .in21(r22), .in22(r23), .in23(r24), .in24(r25), .in25(r26),
    .in26(r27), .in27(r28), .in28(r29), .in29(r30), .in30(r31), .in31(r32), .out(out_9), .sel(A1), .en(1'b1));
  // Probe on out_9
  Multiplexer #(.select(5), .width(32)) multiplexer_2 (
    .in0(r1), .in1(r2), .in2(r3), .in3(r4), .in4(r5), .in5(r6), .in6(r7), .in7(r8), .in8(r9), .in9(r10),
    .in10(r11), .in11(r12), .in12(r13), .in13(r14), .in14(r15), .in15(r16), .in16(r17), .in17(r18),
    .in18(r19), .in19(r20), .in20(r21), .in21(r22), .in22(r23), .in23(r24), .in24(r25), .in25(r26),
    .in26(r27), .in27(r28), .in28(r29), .in29(r30), .in30(r31), .in31(r32), .out(out_8), .sel(A2), .en(1'b1));
  // Probe on WD
  Demultiplexer #(.select(5), .width(32), .tristate("true")) demultiplexer_1 (
    .out0(r_1), .out1(r_2), .out2(r_3), .out3(r_4), .out4(r_5), .out5(r_6), .out6(r_7), .out7(r_8),
    .out8(r_9), .out9(r_10), .out10(r_11), .out11(r_12), .out12(r_13), .out13(r_14), .out14(r_15),
    .out15(r_16), .out16(r_17), .out17(r_18), .out18(r_19), .out19(r_20), .out20(r_21), .out21(r_22),
    .out22(r_23), .out23(r_24), .out24(r_25), .out25(r_26), .out26(r_27), .out27(r_28), .out28(r_29),
    .out29(r_30), .out30(r_31), .out31(r_32), .in(WD), .sel(A3), .en(WE));
  // Probe on r_3

  // Other names for the same wires on the sheet: clk_zu = clk; RD1[31:0] = out_9; RD2[31:0] = out_8
endmodule

module grf2 (
  input  clk,
  input  reset,
  input  WE,
  input  [4:0] A1,
  input  [4:0] A2,
  input  [4:0] A3,
  input  [31:0] WD,
  output [31:0] out_8,
  output [31:0] out_9
);

  wire multiplexer_3_out;
  wire [31:0] r1, r2, r3, r4, r5, r6, r7, r8, r9, r10, r11, r12, r13, r14, r15, r16, r17, r18, r19, r20, r21,
       r22, r23, r24, r25, r26, r27, r28, r29, r30, r31, r32, r_1, r_2, r_3, r_4, r_5, r_6, r_7, r_8, r_9,
       r_10, r_11, r_12, r_13, r_14, r_15, r_16, r_17, r_18, r_19, r_20, r_21, r_22, r_23, r_24, r_25, r_26,
       r_27, r_28, r_29, r_30, r_31, r_32;

  // Probe on r_3
  Register #(.width(32)) register_1 (.Q(r1), .clk(clk), .clr(reset));  // open: D, en
  Register #(.width(32)) register_2 (.D(r_2), .Q(r2), .clk(clk), .clr(reset));  // open: en
  Register #(.width(32)) register_3 (.D(r_3), .Q(r3), .clk(clk), .clr(reset));  // open: en
  Register #(.width(32)) register_4 (.D(r_4), .Q(r4), .clk(clk), .clr(reset));  // open: en
  Register #(.width(32)) register_5 (.D(r_5), .Q(r5), .clk(clk), .clr(reset));  // open: en
  Register #(.width(32)) register_6 (.D(r_6), .Q(r6), .clk(clk), .clr(reset));  // open: en
  Register #(.width(32)) register_7 (.D(r_7), .Q(r7), .clk(clk), .clr(reset));  // open: en
  Register #(.width(32)) register_8 (.D(r_8), .Q(r8), .clk(clk), .clr(reset));  // open: en
  Register #(.width(32)) register_9 (.D(r_9), .Q(r9), .clk(clk), .clr(reset));  // open: en
  Register #(.width(32)) register_10 (.D(r_10), .Q(r10), .clk(clk), .clr(reset));  // open: en
  Register #(.width(32)) register_11 (.D(r_11), .Q(r11), .clk(clk), .clr(reset));  // open: en
  Register #(.width(32)) register_12 (.D(r_12), .Q(r12), .clk(clk), .clr(reset));  // open: en
  Register #(.width(32)) register_13 (.D(r_13), .Q(r13), .clk(clk), .clr(reset));  // open: en
  Register #(.width(32)) register_14 (.D(r_14), .Q(r14), .clk(clk), .clr(reset));  // open: en
  Register #(.width(32)) register_15 (.D(r_15), .Q(r15), .clk(clk), .clr(reset));  // open: en
  Register #(.width(32)) register_16 (.D(r_16), .Q(r16), .clr(reset));  // open: en, clk
  Register #(.width(32)) register_17 (.D(r_17), .Q(r17), .clk(clk), .clr(reset));  // open: en
  Register #(.width(32)) register_18 (.D(r_18), .Q(r18), .clk(clk), .clr(reset));  // open: en
  Register #(.width(32)) register_19 (.D(r_19), .Q(r19), .clk(clk), .clr(reset));  // open: en
  Register #(.width(32)) register_20 (.D(r_20), .Q(r20), .clk(clk), .clr(reset));  // open: en
  Register #(.width(32)) register_21 (.D(r_21), .Q(r21), .clk(clk), .clr(reset));  // open: en
  Register #(.width(32)) register_22 (.D(r_22), .Q(r22), .clk(clk), .clr(reset));  // open: en
  Register #(.width(32)) register_23 (.D(r_23), .Q(r23), .clk(clk), .clr(reset));  // open: en
  Register #(.width(32)) register_24 (.D(r_24), .Q(r24), .clk(clk), .clr(reset));  // open: en
  Register #(.width(32)) register_25 (.D(r_25), .Q(r25), .clk(clk), .clr(reset));  // open: en
  Register #(.width(32)) register_26 (.D(r_26), .Q(r26), .clk(clk), .clr(reset));  // open: en
  Register #(.width(32)) register_27 (.D(r_27), .Q(r27), .clk(clk), .clr(reset));  // open: en
  Register #(.width(32)) register_28 (.D(r_28), .Q(r28), .clk(clk), .clr(reset));  // open: en
  Register #(.width(32)) register_29 (.D(r_29), .Q(r29), .clk(clk), .clr(reset));  // open: en
  Register #(.width(32)) register_30 (.D(r_30), .Q(r30), .clk(clk), .clr(reset));  // open: en
  Register #(.width(32)) register_31 (.D(r_31), .Q(r31), .clk(clk), .clr(reset));  // open: en
  Register #(.width(32)) register_32 (.D(r_32), .Q(r32), .clr(reset));  // open: en, clk
  Multiplexer #(.select(5), .width(32)) multiplexer_1 (
    .in0(r1), .in1(r2), .in2(r3), .in3(r4), .in4(r5), .in5(r6), .in6(r7), .in7(r8), .in8(r9), .in9(r10),
    .in10(r11), .in11(r12), .in12(r13), .in13(r14), .in14(r15), .in15(r16), .in16(r17), .in17(r18),
    .in18(r19), .in19(r20), .in20(r21), .in21(r22), .in22(r23), .in23(r24), .in24(r25), .in25(r26),
    .in26(r27), .in27(r28), .in28(r29), .in29(r30), .in30(r31), .in31(r32), .out(out_9), .sel(A1), .en(1'b1));
  // Probe on out_9
  Multiplexer #(.select(5), .width(32)) multiplexer_2 (
    .in0(r1), .in1(r2), .in2(r3), .in3(r4), .in4(r5), .in5(r6), .in6(r7), .in7(r8), .in8(r9), .in9(r10),
    .in10(r11), .in11(r12), .in12(r13), .in13(r14), .in14(r15), .in15(r16), .in16(r17), .in17(r18),
    .in18(r19), .in19(r20), .in20(r21), .in21(r22), .in22(r23), .in23(r24), .in24(r25), .in25(r26),
    .in26(r27), .in27(r28), .in28(r29), .in29(r30), .in30(r31), .in31(r32), .out(out_8), .sel(A2), .en(1'b1));
  // Probe on WD
  Multiplexer multiplexer_3 (.in0(1'b0), .in1(WE), .out(multiplexer_3_out), .sel(clk));  // open: en
  Demultiplexer #(.select(5), .width(32)) demultiplexer_1 (
    .out0(r_1), .out1(r_2), .out2(r_3), .out3(r_4), .out4(r_5), .out5(r_6), .out6(r_7), .out7(r_8),
    .out8(r_9), .out9(r_10), .out10(r_11), .out11(r_12), .out12(r_13), .out13(r_14), .out14(r_15),
    .out15(r_16), .out16(r_17), .out17(r_18), .out18(r_19), .out19(r_20), .out20(r_21), .out21(r_22),
    .out22(r_23), .out23(r_24), .out24(r_25), .out25(r_26), .out26(r_27), .out27(r_28), .out28(r_29),
    .out29(r_30), .out30(r_31), .out31(r_32), .in(WD), .sel(A3), .en(multiplexer_3_out));
  // Probe on r_3

  // Other names for the same wires on the sheet: clk_zu = clk; RD1[31:0] = out_9; RD2[31:0] = out_8
endmodule
