// Logisim project cpu3.circ as structural Verilog: 11 circuits, main circuit main
module main (
  input  in_1,
  output [31:0] out_2,
  output [31:0] out_3,
  output out_4,
  output [4:0] out_5,
  output [31:0] out_6,
  output out_7,
  output [31:0] out_8,
  output [31:0] out_9
);

  wire and_1_out, clk, contrl1_1_out_2, is_mooez, itype, LW, mooez, nadd_ctrl, R, undriven, zero, zero_EXT_s;
  wire [2:0] ALU_op, op;
  wire [4:0] rd, rs, rt;
  wire [5:0] divider_1_func, divider_1_operation;
  wire [15:0] imm16;
  wire [31:0] adder_2_out, adder_3_out, dm_1_rdata, E_S, EXT, EXT_ans, grf_1_out_8, multiplexer_3_out,
       multiplexer_4_out, pc, zero_EXT;

  Adder #(.width(32)) adder_1 (.a(pc), .b(32'h3000), .out(out_3));  // open: cin, cout
  // Probe on multiplexer_3_out
  Multiplexer #(.width(32)) multiplexer_1 (.in0(EXT), .in1(zero_EXT), .out(EXT_ans), .sel(zero_EXT_s), .en(undriven));
  Clock clock_1 (.out(clk));
  PC pc_1 (.PC_next(multiplexer_3_out), .clk(clk), .rst(in_1), .PC_now(pc));
  // Probe on rs
  IM im_1 (.PC(pc), .instruction(out_2));
  Multiplexer #(.width(5)) multiplexer_2 (.in0(rt), .in1(rd), .out(out_5), .sel(R));  // open: en
  Adder #(.width(32)) adder_2 (.a(32'h4), .b(pc), .out(adder_2_out));  // open: cin, cout
  Divider divider_1 (
    .in_1(out_2), .operation(divider_1_operation), .rs(rs), .rt(rt), .rd(rd), .func(divider_1_func),
    .imm16(imm16));
  contrl1 contrl1_1 (
    .operation(divider_1_operation), .out_2(contrl1_1_out_2), .out_3(R), .out_4(LW), .out_5(itype),
    .out_6(out_4), .out_7(out_7), .ALU_op(ALU_op), .zero_EXT_S(zero_EXT_s), .is_mooez(is_mooez));
  GRF grf_1 (
    .in_1(clk), .reset(in_1), .WE(out_4), .Rreg1(rs), .Rreg2(rt), .Wreg(out_5), .Wdata(out_6),
    .out_8(grf_1_out_8), .out_9(out_9));
  Adder #(.width(32)) adder_3 (.a(adder_2_out), .b(E_S), .out(adder_3_out));  // open: cin, cout
  // Probe on op
  contrl2 contrl2_1 (.funct(divider_1_func), .ALU_op(ALU_op), .out_3(op));
  Multiplexer #(.width(32)) multiplexer_3 (
    .in0(adder_2_out), .in1(adder_3_out), .out(multiplexer_3_out), .sel(and_1_out));  // open: en
  and and_1 (and_1_out, contrl1_1_out_2, nadd_ctrl);
  Multiplexer #(.width(32)) multiplexer_4 (
    .in0(out_9), .in1(EXT_ans), .out(multiplexer_4_out), .sel(itype));  // open: en
  ALU alu_1 (.data1(grf_1_out_8), .data2(multiplexer_4_out), .op(op), .zero(zero), .ans(out_8), .mooez(mooez));
  EXT ext_1 (.in_1(imm16), .out_2(EXT));
  assign zero_EXT = {{16{1'b0}}, imm16};  // Bit_Extender bit_extender_1
  DM dm_1 (.rst(in_1), .adress(out_8), .WE(out_7), .Wdata(out_9), .re(LW), .clk(clk), .Rdata(dm_1_rdata));
  Shifter #(.width(32)) shifter_1 (.in(EXT), .\dist (5'b00010), .out(E_S));
  Multiplexer #(.width(32)) multiplexer_5 (.in0(out_8), .in1(dm_1_rdata), .out(out_6), .sel(LW));  // open: en
  Multiplexer multiplexer_6 (.in0(zero), .in1(mooez), .out(nadd_ctrl), .sel(is_mooez));  // open: en

  // Other names for the same wires on the sheet: DM_WE = out_7; GRF_WE = out_4; instr[31:0] = out_2;
  //   MemAddr[31:0] = out_8; MemData[31:0] = out_9; reset = in_1; Wdata[31:0] = out_6; Wreg[4:0] = out_5
endmodule

module PC (
  input  [31:0] PC_next,
  input  clk,
  input  rst,
  output [31:0] PC_now
);

  Register #(.width(32)) register_1 (.D(PC_next), .Q(PC_now), .clk(clk), .clr(rst));  // open: en
endmodule

module IM (
  input  [31:0] PC,
  output [31:0] instruction
);

  wire [31:0] shifter_1_out;

  Shifter #(.width(32), .shift("ar")) shifter_1 (.in(PC), .\dist (5'b00010), .out(shifter_1_out));
  // Probe on shifter_1_out[13:0]
  ROM #(.addrWidth(14), .dataWidth(32)) rom_1 (.addr(shifter_1_out[13:0]), .data(instruction));  // open: sel

  // Notes on the sheet:
  //   contents of rom_1 (hex, n*v repeats v):
  //   34080010 3610000f ad080004 ad100008 8d090004 8d0a0008 12a5820 1496022 356d000f 3c0effff ad0b0000
  //   ad0c0004 ad0d0008 ad0e000c 1109fff1
endmodule

module GRF (
  input  in_1,
  input  reset,
  input  WE,
  input  [4:0] Rreg1,
  input  [4:0] Rreg2,
  input  [4:0] Wreg,
  input  [31:0] Wdata,
  output [31:0] out_8,
  output [31:0] out_9
);

  wire [31:0] r1, r2, r3, r4, r5, r6, r7, r8, r9, r10, r11, r12, r13, r14, r15, r16, r17, r18, r19, r20, r21,
       r22, r23, r24, r25, r26, r27, r28, r29, r30, r31, r32, r_1, r_2, r_3, r_4, r_5, r_6, r_7, r_8, r_9,
       r_10, r_11, r_12, r_13, r_14, r_15, r_16, r_17, r_18, r_19, r_20, r_21, r_22, r_23, r_24, r_25, r_26,
       r_27, r_28, r_29, r_30, r_31, r_32;

  // Probe on r_3
  Register #(.width(32)) register_1 (.Q(r1), .clk(in_1), .clr(reset));  // open: D, en
  Register #(.width(32)) register_2 (.D(r_2), .Q(r2), .clk(in_1), .clr(reset));  // open: en
  Register #(.width(32)) register_3 (.D(r_3), .Q(r3), .clk(in_1), .clr(reset));  // open: en
  Register #(.width(32)) register_4 (.D(r_4), .Q(r4), .clk(in_1), .clr(reset));  // open: en
  Register #(.width(32)) register_5 (.D(r_5), .Q(r5), .clk(in_1), .clr(reset));  // open: en
  Register #(.width(32)) register_6 (.D(r_6), .Q(r6), .clk(in_1), .clr(reset));  // open: en
  Register #(.width(32)) register_7 (.D(r_7), .Q(r7), .clk(in_1), .clr(reset));  // open: en
  Register #(.width(32)) register_8 (.D(r_8), .Q(r8), .clk(in_1), .clr(reset));  // open: en
  Register #(.width(32)) register_9 (.D(r_9), .Q(r9), .clk(in_1), .clr(reset));  // open: en
  Register #(.width(32)) register_10 (.D(r_10), .Q(r10), .clk(in_1), .clr(reset));  // open: en
  Register #(.width(32)) register_11 (.D(r_11), .Q(r11), .clk(in_1), .clr(reset));  // open: en
  Register #(.width(32)) register_12 (.D(r_12), .Q(r12), .clk(in_1), .clr(reset));  // open: en
  Register #(.width(32)) register_13 (.D(r_13), .Q(r13), .clk(in_1), .clr(reset));  // open: en
  Register #(.width(32)) register_14 (.D(r_14), .Q(r14), .clk(in_1), .clr(reset));  // open: en
  Register #(.width(32)) register_15 (.D(r_15), .Q(r15), .clk(in_1), .clr(reset));  // open: en
  Register #(.width(32)) register_16 (.D(r_16), .Q(r16), .clk(in_1), .clr(reset));  // open: en
  Register #(.width(32)) register_17 (.D(r_17), .Q(r17), .clk(in_1), .clr(reset));  // open: en
  Register #(.width(32)) register_18 (.D(r_18), .Q(r18), .clk(in_1), .clr(reset));  // open: en
  Register #(.width(32)) register_19 (.D(r_19), .Q(r19), .clk(in_1), .clr(reset));  // open: en
  Register #(.width(32)) register_20 (.D(r_20), .Q(r20), .clk(in_1), .clr(reset));  // open: en
  Register #(.width(32)) register_21 (.D(r_21), .Q(r21), .clk(in_1), .clr(reset));  // open: en
  Register #(.width(32)) register_22 (.D(r_22), .Q(r22), .clk(in_1), .clr(reset));  // open: en
  Register #(.width(32)) register_23 (.D(r_23), .Q(r23), .clk(in_1), .clr(reset));  // open: en
  Register #(.width(32)) register_24 (.D(r_24), .Q(r24), .clk(in_1), .clr(reset));  // open: en
  Register #(.width(32)) register_25 (.D(r_25), .Q(r25), .clk(in_1), .clr(reset));  // open: en
  Register #(.width(32)) register_26 (.D(r_26), .Q(r26), .clk(in_1), .clr(reset));  // open: en
  Register #(.width(32)) register_27 (.D(r_27), .Q(r27), .clk(in_1), .clr(reset));  // open: en
  Register #(.width(32)) register_28 (.D(r_28), .Q(r28), .clk(in_1), .clr(reset));  // open: en
  Register #(.width(32)) register_29 (.D(r_29), .Q(r29), .clk(in_1), .clr(reset));  // open: en
  Register #(.width(32)) register_30 (.D(r_30), .Q(r30), .clk(in_1), .clr(reset));  // open: en
  Register #(.width(32)) register_31 (.D(r_31), .Q(r31), .clk(in_1), .clr(reset));  // open: en
  Register #(.width(32)) register_32 (.D(r_32), .Q(r32), .clk(in_1), .clr(reset));  // open: en
  Multiplexer #(.select(5), .width(32)) multiplexer_1 (
    .in0(r1), .in1(r2), .in2(r3), .in3(r4), .in4(r5), .in5(r6), .in6(r7), .in7(r8), .in8(r9), .in9(r10),
    .in10(r11), .in11(r12), .in12(r13), .in13(r14), .in14(r15), .in15(r16), .in16(r17), .in17(r18),
    .in18(r19), .in19(r20), .in20(r21), .in21(r22), .in22(r23), .in23(r24), .in24(r25), .in25(r26),
    .in26(r27), .in27(r28), .in28(r29), .in29(r30), .in30(r31), .in31(r32), .out(out_8), .sel(Rreg1),
    .en(1'b1));
  // Probe on out_8
  Multiplexer #(.select(5), .width(32)) multiplexer_2 (
    .in0(r1), .in1(r2), .in2(r3), .in3(r4), .in4(r5), .in5(r6), .in6(r7), .in7(r8), .in8(r9), .in9(r10),
    .in10(r11), .in11(r12), .in12(r13), .in13(r14), .in14(r15), .in15(r16), .in16(r17), .in17(r18),
    .in18(r19), .in19(r20), .in20(r21), .in21(r22), .in22(r23), .in23(r24), .in24(r25), .in25(r26),
    .in26(r27), .in27(r28), .in28(r29), .in29(r30), .in30(r31), .in31(r32), .out(out_9), .sel(Rreg2),
    .en(1'b1));
  // Probe on Wdata
  Demultiplexer #(.select(5), .width(32), .tristate("true")) demultiplexer_1 (
    .out0(r_1), .out1(r_2), .out2(r_3), .out3(r_4), .out4(r_5), .out5(r_6), .out6(r_7), .out7(r_8),
    .out8(r_9), .out9(r_10), .out10(r_11), .out11(r_12), .out12(r_13), .out13(r_14), .out14(r_15),
    .out15(r_16), .out16(r_17), .out17(r_18), .out18(r_19), .out19(r_20), .out20(r_21), .out21(r_22),
    .out22(r_23), .out23(r_24), .out24(r_25), .out25(r_26), .out26(r_27), .out27(r_28), .out28(r_29),
    .out29(r_30), .out30(r_31), .out31(r_32), .in(Wdata), .sel(Wreg), .en(WE));
  // Probe on r_3

  // Other names for the same wires on the sheet: A1[4:0] = Rreg1; A2[4:0] = Rreg2; A3[4:0] = Wreg; clk_zu = in_1;
  //   RD1[31:0] = out_8; RD2[31:0] = out_9; WD[31:0] = Wdata
endmodule

module ALU (
  input  [31:0] data1,
  input  [31:0] data2,
  input  [2:0] op,
  output zero,
  output [31:0] ans,
  output mooez
);

  wire comparator_1_eq, comparator_2_eq;
  wire [5:0] bitadder_1_out, bitadder_2_out;
  wire [31:0] adder_1_out, and_1_out, multiplier_1_out, multiplier_2_out, not_1_out, or_1_out,
       subtractor_1_out;

  assign not_1_out = ~data2;  // NOT_Gate not_1, 32 bits wide
  Multiplier #(.width(32)) multiplier_1 (.a(data1), .b(data1), .out(multiplier_1_out));  // open: cin, cout
  Multiplier #(.width(32)) multiplier_2 (.a(data2), .b(data2), .out(multiplier_2_out));  // open: cin, cout
  BitAdder #(.width(1)) bitadder_1 (
    .in0(data1[0]), .in1(data1[1]), .in2(data1[2]), .in3(data1[3]), .in4(data1[4]), .in5(data1[5]),
    .in6(data1[6]), .in7(data1[7]), .in8(data1[8]), .in9(data1[9]), .in10(data1[10]), .in11(data1[11]),
    .in12(data1[12]), .in13(data1[13]), .in14(data1[14]), .in15(data1[15]), .in16(data1[16]),
    .in17(data1[17]), .in18(data1[18]), .in19(data1[19]), .in20(data1[20]), .in21(data1[21]),
    .in22(data1[22]), .in23(data1[23]), .in24(data1[24]), .in25(data1[25]), .in26(data1[26]),
    .in27(data1[27]), .in28(data1[28]), .in29(data1[29]), .in30(data1[30]), .in31(data1[31]),
    .out(bitadder_1_out));
  Adder #(.width(32)) adder_1 (.a(data1), .b(data2), .out(adder_1_out));  // open: cin, cout
  Subtractor #(.width(32)) subtractor_1 (.a(data1), .b(data2), .out(subtractor_1_out));  // open: bin, bout
  assign or_1_out = data1 | data2;  // OR_Gate or_1, 32 bits wide
  assign and_1_out = multiplier_1_out & multiplier_2_out;  // AND_Gate and_1, 32 bits wide
  BitAdder #(.width(1)) bitadder_2 (
    .in0(not_1_out[0]), .in1(not_1_out[1]), .in2(not_1_out[2]), .in3(not_1_out[3]), .in4(not_1_out[4]),
    .in5(not_1_out[5]), .in6(not_1_out[6]), .in7(not_1_out[7]), .in8(not_1_out[8]), .in9(not_1_out[9]),
    .in10(not_1_out[10]), .in11(not_1_out[11]), .in12(not_1_out[12]), .in13(not_1_out[13]),
    .in14(not_1_out[14]), .in15(not_1_out[15]), .in16(not_1_out[16]), .in17(not_1_out[17]),
    .in18(not_1_out[18]), .in19(not_1_out[19]), .in20(not_1_out[20]), .in21(not_1_out[21]),
    .in22(not_1_out[22]), .in23(not_1_out[23]), .in24(not_1_out[24]), .in25(not_1_out[25]),
    .in26(not_1_out[26]), .in27(not_1_out[27]), .in28(not_1_out[28]), .in29(not_1_out[29]),
    .in30(not_1_out[30]), .in31(not_1_out[31]), .out(bitadder_2_out));
  // Probe on or_1_out
  Comparator #(.width(1), .mode("unsigned")) comparator_1 (
    .a(bitadder_1_out[0]), .b(1'b1), .eq(comparator_1_eq));  // open: gt, lt
  Comparator #(.width(1), .mode("unsigned")) comparator_2 (
    .a(1'b0), .b(bitadder_2_out[0]), .eq(comparator_2_eq));  // open: gt, lt
  Comparator #(.width(32), .mode("unsigned")) comparator_3 (
    .a({32{1'b0}}), .b(subtractor_1_out), .eq(zero));  // open: gt, lt
  and and_2 (mooez, comparator_1_eq, comparator_2_eq);
  Multiplexer #(.select(3), .width(32)) multiplexer_1 (
    .in0(adder_1_out), .in1(subtractor_1_out), .in2(adder_1_out), .in3(or_1_out),
    .in4({data2[15:0], {16{1'b0}}}), .in5(and_1_out), .out(ans), .sel(op), .en(1'b1));  // open: in6, in7
endmodule

module DM (
  input  rst,
  input  [31:0] adress,
  input  WE,
  input  [31:0] Wdata,
  input  re,
  input  clk,
  output [31:0] Rdata
);

  RAM #(.addrWidth(12), .dataWidth(32), .bus("separate")) ram_1 (
    .addr(adress[13:2]), .din(Wdata), .data(Rdata), .str(WE), .clk(clk), .ld(re), .clr(rst));  // open: sel
endmodule

module EXT (
  input  [15:0] in_1,
  output [31:0] out_2
);

  assign out_2 = {{16{in_1[15]}}, in_1};  // Bit_Extender bit_extender_1
endmodule

module Divider (
  input  [31:0] in_1,
  output [5:0] operation,
  output [4:0] rs,
  output [4:0] rt,
  output [4:0] rd,
  output [5:0] func,
  output [15:0] imm16
);


  assign func = in_1[5:0];
  assign imm16 = in_1[15:0];
  assign operation = in_1[31:26];
  assign rd = in_1[15:11];
  assign rs = in_1[25:21];
  assign rt = in_1[20:16];
endmodule

module contrl1 (
  input  [5:0] operation,
  output out_2,
  output out_3,
  output out_4,
  output out_5,
  output out_6,
  output out_7,
  output [2:0] ALU_op,
  output zero_EXT_S,
  output is_mooez
);

  wire beq, lui, lw, mooez, nop0, nop1, nop2, nop3, nop4, nop5, ori, R, sw;

  not not_1 (nop0, operation[0]);
  not not_2 (nop1, operation[1]);
  not not_3 (nop2, operation[2]);
  not not_4 (nop3, operation[3]);
  not not_5 (nop4, operation[4]);
  not not_6 (nop5, operation[5]);
  or or_1 (out_2, beq, 1'b0, mooez);
  or or_2 (out_3, R, 1'b0);
  or or_3 (out_4, lw, 1'b0);
  or or_4 (out_5, ori, lw, sw, lui);
  or or_5 (out_6, R, ori, lw, lui);
  or or_6 (out_7, sw, 1'b0);
  or or_7 (ALU_op[0], ori, lw, sw);
  or or_8 (ALU_op[1], beq, ori);
  buf or_9 (ALU_op[2], lui);  // OR_Gate
  buf or_10 (is_mooez, mooez);  // OR_Gate
  buf or_11 (zero_EXT_S, ori);  // OR_Gate
  and u_R (R, nop5, nop4, nop3, nop2, nop1, nop0);
  and u_ori (ori, operation[0], nop1, operation[2], operation[3], nop4, nop5);
  and u_lw (lw, operation[0], operation[1], nop2, nop3, nop4, operation[5]);
  and u_sw (sw, operation[0], operation[1], nop2, operation[3], nop4, operation[5]);
  and u_beq (beq, nop0, nop1, operation[2], nop3, nop4, nop5);
  and u_lui (lui, operation[0], operation[1], operation[2], operation[3], nop4, nop5);
  and u_mooez (mooez, nop0, operation[1], nop2, operation[3], nop4, operation[5]);

  // Other names for the same wires on the sheet: op0 = operation[0]; op1 = operation[1]; op2 = operation[2];
  //   op3 = operation[3]; op4 = operation[4]; op5 = operation[5]
endmodule

module contrl2 (
  input  [5:0] funct,
  input  [2:0] ALU_op,
  output [2:0] out_3
);

  wire nf0, nf1, nf2, nf3, nf4, nf5;
  wire [2:0] multiplexer_1_out, select;

  not not_1 (nf0, funct[0]);
  not not_2 (nf1, funct[1]);
  not not_3 (nf2, funct[2]);
  not not_4 (nf3, funct[3]);
  not not_5 (nf4, funct[4]);
  not not_6 (nf5, funct[5]);
  Multiplexer #(.select(4), .width(3)) multiplexer_1 (
    .in0(3'b000), .in1(3'b000), .in2(3'b001), .in4(3'b101), .out(multiplexer_1_out), .sel({1'b0, select}));  // open: in3, in5, in6, in7, in8, in9, in10, in11, in12, in13, in14, in15, en
  Multiplexer #(.select(3), .width(3)) multiplexer_2 (
    .in0(multiplexer_1_out), .in1(3'b000), .in2(3'b010), .in3(3'b011), .in4(3'b100), .out(out_3), .sel(ALU_op));  // open: in5, in6, in7, en
  and add (select[0], funct[5], nf4, nf3, nf2, nf1, nf0);
  and sub (select[1], funct[5], nf4, nf3, nf2, funct[1], nf0);
  and qaq (select[2], nf5, funct[4], nf3, funct[2], funct[1], nf0);

  // Other names for the same wires on the sheet: f0 = funct[0]; f1 = funct[1]; f2 = funct[2]; f3 = funct[3];
  //   f4 = funct[4]; f5 = funct[5]
endmodule

module shift (
  input  [31:0] in_1,
  output [31:0] out_2
);


  assign out_2 = {in_1[29:0], 2'b00};
endmodule
